# Fritzing sketch RaspberryPi3Seguridad (saved by Fritzing 0.9.3b)
breadboards: 1

parts:
  Raspberry_Pi_1 = Raspberry Pi 3 [part_number=RPI-3-V1.2]
  Part1 = RFID-RC522 [part_number=101218]
  LED1 = LED - 5mm [color="Red (633nm)" package="5 mm [THT]"]
  LED2 = LED - 5mm [color="Green (570nm)" package="5 mm [THT]"]
  R1 = Resistor [tolerance=±5% resistance=220 package=THT]
  R2 = Resistor [tolerance=±5% resistance=220 package=THT]

nets:
  3V3: Raspberry_Pi_1.3v3, Part1.3.3V
  N1: Raspberry_Pi_1.GPIO10, Part1.MOSI
  N2: Raspberry_Pi_1.GPIO9, Part1.MISO
  N3: Raspberry_Pi_1.GPIO11, Part1.SCK
  N4: Raspberry_Pi_1.GPIO5, R1.Pin_0
  N5: Raspberry_Pi_1.GPIO6, R2.Pin_0
  N6: Raspberry_Pi_1.GPIO8, Part1.SDA
  N7: Raspberry_Pi_1.GPIO25, Part1.RST
  GND: Raspberry_Pi_1.GND, Part1.GND, LED1.cathode, LED2.cathode
  N8: LED1.anode, R1.Pin_1
  N9: LED2.anode, R2.Pin_1
