# Fritzing sketch arduino1 (saved by Fritzing 0.9.10b)
breadboards: 1

parts:
  Componente1 = Arduino Uno (Rev3) - ICSP
  RHT1 = Humidity and Temperature Sensor RHT03  # not connected
  Water_Level_Sensor1 = Water Level Sensor
  PIR1 = PIR sensor  # not connected
  P1 = S1133 Si Photodiode [package="8mm Ceramic [THT]"]  # not connected
  LED1 = RGB LED - (4 legs) [package="5 mm [THT]"]  # not connected

nets:
  N1: Componente1.D4, Water_Level_Sensor1.SIG
  5V: Componente1.5V, Water_Level_Sensor1.VCC
  GND: Componente1.GND, Water_Level_Sensor1.GND

custom parts:
  Water Level Sensor: A water level sensor. This sensor operates at 3V to 5V. The Sig (signal) pin outputs an analogue signal that is in proportion to the amount of water in contact with the sensor.
