# Fritzing sketch rpizero (saved by Fritzing 0.9.10b)
breadboards: 1

parts:
  MCU1 = Raspberry Pi Zero
  LCD1 = LCD screen  # not connected
  Componente1 = RFID-RC522-v2  # not connected
  LED1 = LED - 5mm [color="Red (633nm)" current=0.030 package="5 mm [THT]"]
  LED2 = LED - 5mm [color="Green (570nm)" current=0.030 package="5 mm [THT]"]
  PIR1 = PIR sensor
  LED3 = LED - 5mm [color="White (8000K)" current=30mA package="5 mm [THT]"]

nets:
  N1: MCU1.pin_2, MCU1.pin_4, PIR1.GND
  N2: MCU1.pin_6, MCU1.pin_9, MCU1.pin_14, MCU1.pin_16, MCU1.pin_30, MCU1.pin_34, LED1.cathode, PIR1.SIG
  N3: MCU1.pin_18, MCU1.pin_31, LED3.anode
  N4: MCU1.pin_38, LED2.anode

custom parts:
  RFID-RC522-v2: A simple China made RFID-RC522 Reader; do check the pin labels, as this is a MFRC522 based clone.
